# Fritzing sketch Weather Station OLED (saved by Fritzing 0.9.3b)
circuit board: 7.92888cm x 5.64444cm

parts:
  J1 = male pin header, 3 pins [form="♂ (male)"]
  U1 = NodeMCU V1.0
  Squix1 = OLED 0.96" 128x64 I2C SSD1306

nets (from the breadboard view):
  N1: J1.pin1, U1.D6
  3V3: J1.pin2, U1.3V3, Squix1.VCC
  GND: J1.pin3, U1.GND, Squix1.GND
  N2: U1.D3, Squix1.SCA
  N3: U1.D5, Squix1.SCL

notes:
  Weather Station Schematic

custom parts:
  NodeMCU V1.0: ESP8266 based NodeMCU
